# Fritzing sketch wireless_temp_RX (saved by Fritzing 0.9.2b)
breadboards: 1

parts:
  NRF24L1 = NRF24L01
  Eleman1 = Arduino Uno (Rev3)
  LCD1 = LCD screen
  R1 = Trimmer Potentiometer [maximum_resistance=10kΩ package=THT]

nets:
  VCC: NRF24L1.VCC, Eleman1.3V3
  N1: NRF24L1.CSN, Eleman1.D8
  N2: NRF24L1.MOSI, Eleman1.D11_PWM/MOSI
  GND: NRF24L1.GND, Eleman1.GND, LCD1.VSS, R1.leg2
  N3: NRF24L1.CE, Eleman1.D7
  N4: NRF24L1.SCK, Eleman1.D13/SCK
  N5: NRF24L1.MISO, Eleman1.D12/MISO
  N6: Eleman1.D9_PWM, LCD1.E
  N7: Eleman1.D10_PWM/SS, LCD1.RS
  N8: Eleman1.D2, LCD1.DB4
  N9: Eleman1.D3_PWM, LCD1.DB5
  N10: Eleman1.D4, LCD1.DB6
  N11: Eleman1.D5_PWM, LCD1.DB7
  5V: Eleman1.5V, LCD1.VDD, R1.leg1
  N12: LCD1.V0, R1.wiper

custom parts:
  NRF24L01: NRF24L01 module
