# Fritzing sketch wireless_temp_TX (saved by Fritzing 0.9.2b)
breadboards: 1

parts:
  NRF24L1 = NRF24L01
  Eleman1 = Arduino Uno (Rev3)
  DHT1 = DHT11 Humitidy and Temperature Sensor

nets:
  VCC: NRF24L1.VCC, Eleman1.3V3
  N1: NRF24L1.CSN, Eleman1.D10_PWM/SS
  N2: NRF24L1.MOSI, Eleman1.D11_PWM/MOSI
  GND: NRF24L1.GND, Eleman1.GND, DHT1.GND
  N3: NRF24L1.CE, Eleman1.D9_PWM
  N4: NRF24L1.SCK, Eleman1.D13/SCK
  N5: NRF24L1.MISO, Eleman1.D12/MISO
  N6: Eleman1.A0, DHT1.DATA
  5V: Eleman1.5V, DHT1.VDD

custom parts:
  NRF24L01: NRF24L01 module
  DHT11 Humitidy and Temperature Sensor: DHT11 Humidity and Temperature Sensor
